// Logisim project pc.circ as structural Verilog: 9 circuits, main circuit main
module main (
);

  wire ALUO, and_1_out, and_2_out, ANDO, CLK, CO, DO, eightbitadder_1_co, Flags, INSTRHO, INSTRLO, IO, JC,
       JMP, JZ, MO, NANDO, nor_1_out, not_1_out, NOTO, or_1_out, RO, SA, SB, SC, SD, SEO,
       sevensegmentdriver_1_a, sevensegmentdriver_1_b, sevensegmentdriver_1_c, sevensegmentdriver_1_d,
       sevensegmentdriver_1_e, sevensegmentdriver_1_f, sevensegmentdriver_1_g, sevensegmentdriver_2_a,
       sevensegmentdriver_2_b, sevensegmentdriver_2_c, sevensegmentdriver_2_d, sevensegmentdriver_2_e,
       sevensegmentdriver_2_f, sevensegmentdriver_2_g, sevensegmentdriver_3_a, sevensegmentdriver_3_b,
       sevensegmentdriver_3_c, sevensegmentdriver_3_d, sevensegmentdriver_3_e, sevensegmentdriver_3_f,
       sevensegmentdriver_3_g, SFLAGS, shift_register_1_p6, shift_register_1_p7, SM, SO, SPO, SRAL, SRAU,
       SROMAL, SROMAU, SSE, SSP;
  wire [3:0] countr_1_q, doubledabble_1_hundreds, doubledabble_1_ones, doubledabble_1_tens;
  wire [5:0] shift_register_1_p8;
  wire [6:0] Flags_q;
  wire [7:0] and_3_out, ARegister_q, BRegister_q, controlled_buffer_1_out, countr_1_q_2, CRegister_q,
       decodr_1_data, dipswitch_1_p1, DRegister_q, eightbitadder_1_sum, nand_1_out, not_2_out,
       OutputRegister, ram_1_dout, RAMAddresRegisterLower_q, RAMAddresRegisterUpper_q, StackEnd_q,
       StackPointer_q;
  wire [15:0] decodr_1_oflags, rom_1_data, ROMAddress;

  TTY tty_1 (.data(OutputRegister[6:0]), .clk(OutputRegister[7]), .we(1'b1), .clr(1'b0));
  Clock clock_1 (.out(CLK));
  _7_Segment_Display u_7_segment_display_1 (
    .g(sevensegmentdriver_1_g), .f(sevensegmentdriver_1_f), .a(sevensegmentdriver_1_a),
    .b(sevensegmentdriver_1_b), .e(sevensegmentdriver_1_e), .d(sevensegmentdriver_1_d),
    .c(sevensegmentdriver_1_c));  // open: dp
  _7_Segment_Display u_7_segment_display_2 (
    .g(sevensegmentdriver_2_g), .f(sevensegmentdriver_2_f), .a(sevensegmentdriver_2_a),
    .b(sevensegmentdriver_2_b), .e(sevensegmentdriver_2_e), .d(sevensegmentdriver_2_d),
    .c(sevensegmentdriver_2_c));  // open: dp
  _7_Segment_Display u_7_segment_display_3 (
    .g(sevensegmentdriver_3_g), .f(sevensegmentdriver_3_f), .a(sevensegmentdriver_3_a),
    .b(sevensegmentdriver_3_b), .e(sevensegmentdriver_3_e), .d(sevensegmentdriver_3_d),
    .c(sevensegmentdriver_3_c));  // open: dp
  SevenSegmentDriver sevensegmentdriver_1 (
    .in_1(doubledabble_1_hundreds), .F(sevensegmentdriver_1_f), .G(sevensegmentdriver_1_g),
    .A(sevensegmentdriver_1_a), .B(sevensegmentdriver_1_b), .C(sevensegmentdriver_1_c),
    .D(sevensegmentdriver_1_d), .E(sevensegmentdriver_1_e));
  SevenSegmentDriver sevensegmentdriver_2 (
    .in_1(doubledabble_1_tens), .F(sevensegmentdriver_2_f), .G(sevensegmentdriver_2_g),
    .A(sevensegmentdriver_2_a), .B(sevensegmentdriver_2_b), .C(sevensegmentdriver_2_c),
    .D(sevensegmentdriver_2_d), .E(sevensegmentdriver_2_e));
  // Probe on {countr_1_q, countr_1_q_2}
  SevenSegmentDriver sevensegmentdriver_3 (
    .in_1(doubledabble_1_ones), .F(sevensegmentdriver_3_f), .G(sevensegmentdriver_3_g),
    .A(sevensegmentdriver_3_a), .B(sevensegmentdriver_3_b), .C(sevensegmentdriver_3_c),
    .D(sevensegmentdriver_3_d), .E(sevensegmentdriver_3_e));
  DoubleDabble doubledabble_1 (
    .in_1(OutputRegister), .Ones(doubledabble_1_ones), .Tens(doubledabble_1_tens),
    .Hundreds(doubledabble_1_hundreds));
  // DipSwitch dipswitch_1: pin names not known; wires that end beside it: dipswitch_1_p1[0], dipswitch_1_p1[1], dipswitch_1_p1[2], dipswitch_1_p1[3], dipswitch_1_p1[4], dipswitch_1_p1[5], dipswitch_1_p1[6], dipswitch_1_p1[7]
  and and_1 (and_1_out, JZ, nor_1_out);
  and and_2 (and_2_out, JC, eightbitadder_1_co);
  or or_1 (or_1_out, JMP, and_1_out, and_2_out);
  not not_1 (not_1_out, CLK);
  assign controlled_buffer_1_out = INSTRHO ? countr_1_q_2 : 8'bz;  // Controlled_Buffer controlled_buffer_1
  assign controlled_buffer_1_out = INSTRLO ? {4'b0000, countr_1_q} : 8'bz;  // Controlled_Buffer controlled_buffer_2
  assign controlled_buffer_1_out = IO ? dipswitch_1_p1 : 8'bz;  // Controlled_Buffer controlled_buffer_3
  nor nor_1 (nor_1_out, controlled_buffer_1_out[7], controlled_buffer_1_out[6], controlled_buffer_1_out[5], controlled_buffer_1_out[4], controlled_buffer_1_out[3], controlled_buffer_1_out[2], controlled_buffer_1_out[1], controlled_buffer_1_out[0]);
  countr countr_1 (.LOAD(or_1_out), .CLK(not_1_out), .P(ROMAddress[11:0]), .Q({countr_1_q, countr_1_q_2}));
  Pull_Resistor pull_resistor_1 (.node(controlled_buffer_1_out[6]));
  Pull_Resistor pull_resistor_2 (.node(controlled_buffer_1_out[5]));
  Pull_Resistor pull_resistor_3 (.node(controlled_buffer_1_out[4]));
  Pull_Resistor pull_resistor_4 (.node(controlled_buffer_1_out[3]));
  Pull_Resistor pull_resistor_5 (.node(controlled_buffer_1_out[7]));
  Pull_Resistor pull_resistor_6 (.node(controlled_buffer_1_out[2]));
  Pull_Resistor pull_resistor_7 (.node(controlled_buffer_1_out[1]));
  Pull_Resistor pull_resistor_8 (.node(controlled_buffer_1_out[0]));
  ROM #(.addrWidth(12), .dataWidth(16)) rom_1 (.addr({countr_1_q, countr_1_q_2}), .data(rom_1_data));
  assign controlled_buffer_1_out = RO ? decodr_1_data : 8'bz;  // Controlled_Buffer controlled_buffer_4
  assign controlled_buffer_1_out = ALUO ? eightbitadder_1_sum : 8'bz;  // Controlled_Buffer controlled_buffer_5
  assign controlled_buffer_1_out = CO ? CRegister_q : 8'bz;  // Controlled_Buffer controlled_buffer_6
  assign controlled_buffer_1_out = DO ? DRegister_q : 8'bz;  // Controlled_Buffer controlled_buffer_7
  assign controlled_buffer_1_out = MO ? ram_1_dout : 8'bz;  // Controlled_Buffer controlled_buffer_8
  assign controlled_buffer_1_out = SPO ? StackPointer_q : 8'bz;  // Controlled_Buffer controlled_buffer_9
  assign controlled_buffer_1_out = SEO ? StackEnd_q : 8'bz;  // Controlled_Buffer controlled_buffer_10
  EightBitRegstr ARegister (.Data(controlled_buffer_1_out), .CLK(CLK), .Store(SA), .Q(ARegister_q));
  EightBitRegstr BRegister (.Data(controlled_buffer_1_out), .CLK(CLK), .Store(SB), .Q(BRegister_q));
  EightBitRegstr CRegister (.Data(controlled_buffer_1_out), .CLK(CLK), .Store(SC), .Q(CRegister_q));
  EightBitRegstr DRegister (.Data(controlled_buffer_1_out), .CLK(CLK), .Store(SD), .Q(DRegister_q));
  EightBitRegstr RAMAddresRegisterLower (
    .Data(controlled_buffer_1_out), .CLK(CLK), .Store(SRAL), .Q(RAMAddresRegisterLower_q));
  EightBitRegstr RAMAddresRegisterUpper (
    .Data(controlled_buffer_1_out), .CLK(CLK), .Store(SRAU), .Q(RAMAddresRegisterUpper_q));
  EightBitRegstr ORegister (.Data(controlled_buffer_1_out), .CLK(CLK), .Store(SO), .Q(OutputRegister));
  EightBitRegstr ROMAddressUpper (.Data(controlled_buffer_1_out), .CLK(CLK), .Store(SROMAU), .Q(ROMAddress[7:0]));
  EightBitRegstr ROMAddressLower (.Data(controlled_buffer_1_out), .CLK(CLK), .Store(SROMAL), .Q(ROMAddress[15:8]));
  EightBitRegstr u_Flags (.Data(controlled_buffer_1_out), .CLK(CLK), .Store(SFLAGS), .Q({Flags, Flags_q}));
  EightBitRegstr StackPointer (.Data(controlled_buffer_1_out), .CLK(CLK), .Store(SSP), .Q(StackPointer_q));
  EightBitRegstr StackEnd (.Data(controlled_buffer_1_out), .CLK(CLK), .Store(SSE), .Q(StackEnd_q));
  assign nand_1_out = ~(ARegister_q & BRegister_q);  // NAND_Gate nand_1, 8 bits wide
  assign not_2_out = ~ARegister_q;  // NOT_Gate not_2, 8 bits wide
  assign and_3_out = ARegister_q & BRegister_q;  // AND_Gate and_3, 8 bits wide
  decodr decodr_1 (
    .in_1(rom_1_data),
    .SFlags({JZ, SFLAGS, SROMAU, SROMAL, SO, JC, JMP, SM, SRAU, SRAL, SD, SC, SSE, SSP, SB, SA}),
    .OFlags({decodr_1_oflags[15], IO, INSTRLO, INSTRHO, ANDO, NOTO, NANDO, MO, SEO, SPO, DO, CO, ALUO, RO, decodr_1_oflags[1:0]}),
    .Data(decodr_1_data));
  assign controlled_buffer_1_out = NANDO ? nand_1_out : 8'bz;  // Controlled_Buffer controlled_buffer_11
  assign controlled_buffer_1_out = NOTO ? not_2_out : 8'bz;  // Controlled_Buffer controlled_buffer_12
  assign controlled_buffer_1_out = ANDO ? and_3_out : 8'bz;  // Controlled_Buffer controlled_buffer_13
  EightBitAdder eightbitadder_1 (
    .A(ARegister_q), .B(BRegister_q), .Subtract(Flags), .Cin(1'b0), .Co(eightbitadder_1_co),
    .SUM(eightbitadder_1_sum));
  RAM #(.addrWidth(16), .enables("line")) ram_1 (
    .addr({RAMAddresRegisterLower_q, RAMAddresRegisterUpper_q}), .we(SM), .clk(CLK),
    .din(controlled_buffer_1_out), .dout(ram_1_dout));
  // Shift_Register #(.length(3), .width(6)) shift_register_1: pin names not known; wires that end beside it: 1'b0, 1'b0, 1'b1, OutputRegister[6], OutputRegister[5:0], shift_register_1_p6, shift_register_1_p7, shift_register_1_p8
  // RGB_Video #(.cursor("No Cursor"), .height(64), .scale(8), .width(64)) rgb_video_1: pin names not known; wires that end beside it: 1'b0, OutputRegister[7], 1'b1, shift_register_1_p6, shift_register_1_p7, shift_register_1_p8[2:0]

  // Notes on the sheet:
  //   contents of rom_1 (hex, n*v repeats v):
  //   e2 ff07 112 ff33 ff07 112 ff33 ff73 1082 ff07 112 ff33 ff73 282 25d2 ff9f ff07 112 ff33 ff73 1782
  //   5ad2 ff9f 80e2 ff07 112 ff33 e2 80e2 ff77 ffd8 80e2 ff07 112 ff33 e2 ff9f e2 ff07 112 ff33 ff07 112
  //   ff33 ff73 3a82 80e2 ff07 212 ff73 e2 ff48 112 ff33 ff77 ff84 4bd2 ff9f 80e2 ff07 112 ff33 e2 80e2
  //   ff07 112 ff33 ff77 ffd8 80e2 ff07 112 ff33 e2 ff9f ff77 ffb8 80e2 ff07 112 ff33 e2 ff77 ffd8 80e2
  //   ff07 112 ff33 e2 ff9f ff9f
  //   ALU
endmodule

module countr (
  input  LOAD,
  input  CLK,
  input  [11:0] P,
  output [11:0] Q
);

  wire CARRY1, CARRY2, n74161_1_pin1, n74161_1_pin7, n74161_1_pin10, n74161_2_pin1, n74161_2_pin10,
       n74161_3_pin1, n74161_3_pin7, n74161_3_pin10, SPE;

  not not_1 (SPE, LOAD);
  _74161 u_74161_1 (
    .pin1(n74161_1_pin1), .pin2(CLK), .pin3(P[0]), .pin4(P[1]), .pin5(P[2]), .pin6(P[3]),
    .pin7(n74161_1_pin7), .pin15(CARRY1), .pin14(Q[0]), .pin13(Q[1]), .pin12(Q[2]), .pin11(Q[3]),
    .pin10(n74161_1_pin10), .pin9(SPE));
  _74161 u_74161_2 (
    .pin1(n74161_2_pin1), .pin2(CLK), .pin3(P[4]), .pin4(P[5]), .pin5(P[6]), .pin6(P[7]), .pin7(CARRY1),
    .pin15(CARRY2), .pin14(Q[4]), .pin13(Q[5]), .pin12(Q[6]), .pin11(Q[7]), .pin10(n74161_2_pin10), .pin9(SPE));
  _74161 u_74161_3 (
    .pin1(n74161_3_pin1), .pin2(CLK), .pin3(P[8]), .pin4(P[9]), .pin5(P[10]), .pin6(P[11]),
    .pin7(n74161_3_pin7), .pin14(Q[8]), .pin13(Q[9]), .pin12(Q[10]), .pin11(Q[11]), .pin10(n74161_3_pin10),
    .pin9(SPE));  // open: pin15
  and and_1 (n74161_3_pin7, CARRY1, CARRY2);
  // also tied to VCC on the sheet: {n74161_1_pin1, n74161_1_pin10, n74161_1_pin7, n74161_2_pin1, n74161_2_pin10, n74161_3_pin1, n74161_3_pin10}

  // Notes on the sheet:
  //   LOAD: pull=up
  //   CLK: pull=up
endmodule

module SevenSegmentDriver (
  input  [3:0] in_1,
  output F,
  output G,
  output A,
  output B,
  output C,
  output D,
  output E
);

  wire n7447_1_pin9, n7447_1_pin10, n7447_1_pin11, n7447_1_pin12, n7447_1_pin13, n7447_1_pin14, n7447_1_pin15;

  not not_1 (F, n7447_1_pin15);
  _7447 u_7447_1 (
    .pin1(in_1[1]), .pin2(in_1[2]), .pin6(in_1[3]), .pin7(in_1[0]), .pin15(n7447_1_pin15),
    .pin14(n7447_1_pin14), .pin13(n7447_1_pin13), .pin12(n7447_1_pin12), .pin11(n7447_1_pin11),
    .pin10(n7447_1_pin10), .pin9(n7447_1_pin9));  // open: pin3, pin4, pin5
  not not_2 (G, n7447_1_pin14);
  not not_3 (A, n7447_1_pin13);
  not not_4 (B, n7447_1_pin12);
  not not_5 (C, n7447_1_pin11);
  not not_6 (D, n7447_1_pin10);
  not not_7 (E, n7447_1_pin9);
endmodule

module DoubleDabble (
  input  [7:0] in_1,
  output [3:0] Ones,
  output [3:0] Tens,
  output [3:0] Hundreds
);

  wire sevensegmentdriver_1_a, sevensegmentdriver_1_b, sevensegmentdriver_1_c, sevensegmentdriver_1_d,
       sevensegmentdriver_1_e, sevensegmentdriver_1_f, sevensegmentdriver_1_g, sevensegmentdriver_2_a,
       sevensegmentdriver_2_b, sevensegmentdriver_2_c, sevensegmentdriver_2_d, sevensegmentdriver_2_e,
       sevensegmentdriver_2_f, sevensegmentdriver_2_g, sevensegmentdriver_3_a, sevensegmentdriver_3_b,
       sevensegmentdriver_3_c, sevensegmentdriver_3_d, sevensegmentdriver_3_e, sevensegmentdriver_3_f,
       sevensegmentdriver_3_g;
  wire [7:4] rom_2_data;

  ROM #(.addrWidth(13)) rom_1 (.addr({{5{1'b0}}, in_1}), .data({Tens, Ones}));
  ROM #(.addrWidth(13), .misaligned("true")) rom_2 (.addr({{5{1'b0}}, in_1}), .data({rom_2_data, Hundreds}));
  _7_Segment_Display u_7_segment_display_1 (
    .g(sevensegmentdriver_1_g), .f(sevensegmentdriver_1_f), .a(sevensegmentdriver_1_a),
    .b(sevensegmentdriver_1_b), .e(sevensegmentdriver_1_e), .d(sevensegmentdriver_1_d),
    .c(sevensegmentdriver_1_c));  // open: dp
  _7_Segment_Display u_7_segment_display_2 (
    .g(sevensegmentdriver_2_g), .f(sevensegmentdriver_2_f), .a(sevensegmentdriver_2_a),
    .b(sevensegmentdriver_2_b), .e(sevensegmentdriver_2_e), .d(sevensegmentdriver_2_d),
    .c(sevensegmentdriver_2_c));  // open: dp
  SevenSegmentDriver sevensegmentdriver_1 (
    .in_1(Hundreds), .F(sevensegmentdriver_1_f), .G(sevensegmentdriver_1_g), .A(sevensegmentdriver_1_a),
    .B(sevensegmentdriver_1_b), .C(sevensegmentdriver_1_c), .D(sevensegmentdriver_1_d),
    .E(sevensegmentdriver_1_e));
  _7_Segment_Display u_7_segment_display_3 (
    .g(sevensegmentdriver_3_g), .f(sevensegmentdriver_3_f), .a(sevensegmentdriver_3_a),
    .b(sevensegmentdriver_3_b), .e(sevensegmentdriver_3_e), .d(sevensegmentdriver_3_d),
    .c(sevensegmentdriver_3_c));  // open: dp
  SevenSegmentDriver sevensegmentdriver_2 (
    .in_1(Tens), .F(sevensegmentdriver_2_f), .G(sevensegmentdriver_2_g), .A(sevensegmentdriver_2_a),
    .B(sevensegmentdriver_2_b), .C(sevensegmentdriver_2_c), .D(sevensegmentdriver_2_d),
    .E(sevensegmentdriver_2_e));
  SevenSegmentDriver sevensegmentdriver_3 (
    .in_1(Ones), .F(sevensegmentdriver_3_f), .G(sevensegmentdriver_3_g), .A(sevensegmentdriver_3_a),
    .B(sevensegmentdriver_3_b), .C(sevensegmentdriver_3_c), .D(sevensegmentdriver_3_d),
    .E(sevensegmentdriver_3_e));

  // Notes on the sheet:
  //   in_1: pull=down
  //   Ones: pull=down
  //   Tens: pull=down
  //   Hundreds: pull=down
  //   contents of rom_1 (hex, n*v repeats v):
  //   0 1 2 3 4 5 6 7 8 9 10 11 12 13 14 15 16 17 18 19 20 21 22 23 24 25 26 27 28 29 30 31 32 33 34 35 36
  //   37 38 39 40 41 42 43 44 45 46 47 48 49 50 51 52 53 54 55 56 57 58 59 60 61 62 63 64 65 66 67 68 69
  //   70 71 72 73 74 75 76 77 78 79 80 81 82 83 84 85 86 87 88 89 90 91 92 93 94 95 96 97 98 99 0 1 2 3 4
  //   5 6 7 8 9 10 11 12 13 14 15 16 17 18 19 20 21 22 23 24 25 26 27 28 29 30 31 32 33 34 35 36 37 38 39
  //   40 41 42 43 44 45 46 47 48 49 50 51 52 53 54 55 56 57 58 59 60 61 62 63 64 65 66 67 68 69 70 71 72
  //   73 74 75 76 77 78 79 80 81 82 83 84 85 86 87 88 89 90 91 92 93 94 95 96 97 98 99 0 1 2 3 4 5 6 7 8 9
  //   10 11 12 13 14 15 16 17 18 19 20 21 22 23 24 25 26 27 28 29 30 31 32 33 34 35 36 37 38 39 40 41 42
  //   43 44 45 46 47 48 49 50 51 52 53 54 55
  //   contents of rom_2 (hex, n*v repeats v):
  //   100*0 100*1 56*2
endmodule

module EightBitRegstr (
  input  [7:0] Data,
  input  CLK,
  input  Store,
  output [7:0] Q
);

  wire controlled_buffer_1_out, controlled_buffer_2_out, controlled_buffer_3_out, controlled_buffer_4_out,
       controlled_buffer_5_out, controlled_buffer_6_out, controlled_buffer_7_out, controlled_buffer_8_out,
       d_ff_1_qn, d_ff_2_qn, d_ff_3_qn, d_ff_4_qn, d_ff_5_qn, d_ff_6_qn, d_ff_7_qn, d_ff_8_qn, not_2_out,
       not_3_out, not_4_out, not_5_out, not_6_out, not_7_out, not_8_out, not_9_out, Store_t;

  not not_1 (Store_t, Store);
  assign controlled_buffer_1_out = not_2_out ? Data[7] : 1'bz;  // Controlled_Buffer controlled_buffer_1
  not not_2 (not_2_out, Store_t);
  assign controlled_buffer_1_out = Store_t ? ~d_ff_1_qn : 1'bz;  // Controlled_Inverter controlled_inverter_1
  D_Flip_Flop d_ff_1 (.clk(CLK), .D(controlled_buffer_1_out), .Q(Q[7]), .Qn(d_ff_1_qn));  // open: preset, reset
  assign controlled_buffer_2_out = not_3_out ? Data[6] : 1'bz;  // Controlled_Buffer controlled_buffer_2
  not not_3 (not_3_out, Store_t);
  assign controlled_buffer_2_out = Store_t ? ~d_ff_2_qn : 1'bz;  // Controlled_Inverter controlled_inverter_2
  D_Flip_Flop d_ff_2 (.clk(CLK), .D(controlled_buffer_2_out), .Q(Q[6]), .Qn(d_ff_2_qn));  // open: preset, reset
  assign controlled_buffer_3_out = not_4_out ? Data[5] : 1'bz;  // Controlled_Buffer controlled_buffer_3
  not not_4 (not_4_out, Store_t);
  assign controlled_buffer_3_out = Store_t ? ~d_ff_3_qn : 1'bz;  // Controlled_Inverter controlled_inverter_3
  D_Flip_Flop d_ff_3 (.clk(CLK), .D(controlled_buffer_3_out), .Q(Q[5]), .Qn(d_ff_3_qn));  // open: preset, reset
  assign controlled_buffer_4_out = not_5_out ? Data[4] : 1'bz;  // Controlled_Buffer controlled_buffer_4
  not not_5 (not_5_out, Store_t);
  assign controlled_buffer_4_out = Store_t ? ~d_ff_4_qn : 1'bz;  // Controlled_Inverter controlled_inverter_4
  D_Flip_Flop d_ff_4 (.clk(CLK), .D(controlled_buffer_4_out), .Q(Q[4]), .Qn(d_ff_4_qn));  // open: preset, reset
  assign controlled_buffer_5_out = not_6_out ? Data[3] : 1'bz;  // Controlled_Buffer controlled_buffer_5
  not not_6 (not_6_out, Store_t);
  assign controlled_buffer_5_out = Store_t ? ~d_ff_5_qn : 1'bz;  // Controlled_Inverter controlled_inverter_5
  D_Flip_Flop d_ff_5 (.clk(CLK), .D(controlled_buffer_5_out), .Q(Q[3]), .Qn(d_ff_5_qn));  // open: preset, reset
  assign controlled_buffer_6_out = not_7_out ? Data[2] : 1'bz;  // Controlled_Buffer controlled_buffer_6
  not not_7 (not_7_out, Store_t);
  assign controlled_buffer_6_out = Store_t ? ~d_ff_6_qn : 1'bz;  // Controlled_Inverter controlled_inverter_6
  D_Flip_Flop d_ff_6 (.clk(CLK), .D(controlled_buffer_6_out), .Q(Q[2]), .Qn(d_ff_6_qn));  // open: preset, reset
  assign controlled_buffer_7_out = not_8_out ? Data[1] : 1'bz;  // Controlled_Buffer controlled_buffer_7
  not not_8 (not_8_out, Store_t);
  assign controlled_buffer_7_out = Store_t ? ~d_ff_7_qn : 1'bz;  // Controlled_Inverter controlled_inverter_7
  D_Flip_Flop d_ff_7 (.clk(CLK), .D(controlled_buffer_7_out), .Q(Q[1]), .Qn(d_ff_7_qn));  // open: preset, reset
  assign controlled_buffer_8_out = not_9_out ? Data[0] : 1'bz;  // Controlled_Buffer controlled_buffer_8
  not not_9 (not_9_out, Store_t);
  assign controlled_buffer_8_out = Store_t ? ~d_ff_8_qn : 1'bz;  // Controlled_Inverter controlled_inverter_8
  D_Flip_Flop d_ff_8 (.clk(CLK), .D(controlled_buffer_8_out), .Q(Q[0]), .Qn(d_ff_8_qn));  // open: preset, reset
endmodule

module EightBitAdder (
  input  [7:0] A,
  input  [7:0] B,
  input  Subtract,
  input  Cin,
  output Co,
  output [7:0] SUM
);

  wire n74283_1_pin9, not_1_out, or_1_out;
  wire [3:0] B_1, controlled_inverter_1_out;

  not not_1 (not_1_out, or_1_out);
  or or_1 (or_1_out, Subtract, Cin);
  assign {B_1, controlled_inverter_1_out} = or_1_out ? ~B : 8'bz;  // Controlled_Inverter controlled_inverter_1
  assign {B_1, controlled_inverter_1_out} = not_1_out ? B : 8'bz;  // Controlled_Buffer controlled_buffer_1
  _74283 u_74283_1 (
    .pin1(SUM[1]), .pin2(A[1]), .pin3(controlled_inverter_1_out[1]), .pin4(SUM[0]),
    .pin5(controlled_inverter_1_out[0]), .pin6(A[0]), .pin7(or_1_out), .pin15(A[2]),
    .pin14(controlled_inverter_1_out[2]), .pin13(SUM[2]), .pin12(controlled_inverter_1_out[3]), .pin11(A[3]),
    .pin10(SUM[3]), .pin9(n74283_1_pin9));
  _74283 u_74283_2 (
    .pin1(SUM[5]), .pin2(A[5]), .pin3(B_1[1]), .pin4(SUM[4]), .pin5(B_1[0]), .pin6(A[4]),
    .pin7(n74283_1_pin9), .pin15(A[6]), .pin14(B_1[2]), .pin13(SUM[6]), .pin12(B_1[3]), .pin11(A[7]),
    .pin10(SUM[7]), .pin9(Co));

  // Other names for the same wires on the sheet: B_2[3:0] = A[7:4]
endmodule

module decodr (
  input  [15:0] in_1,
  output [15:0] SFlags,
  output [15:0] OFlags,
  output [7:0] Data
);

  Decoder #(.disabled("Z"), .enable("false"), .select(4)) decoder_1 (
    .out0(SFlags[0]), .out1(SFlags[1]), .out2(SFlags[2]), .out3(SFlags[3]), .out4(SFlags[4]),
    .out5(SFlags[5]), .out6(SFlags[6]), .out7(SFlags[7]), .out8(SFlags[8]), .out9(SFlags[9]),
    .out10(SFlags[10]), .out11(SFlags[11]), .out12(SFlags[12]), .out13(SFlags[13]), .out14(SFlags[14]),
    .out15(SFlags[15]), .sel(in_1[7:4]));
  Decoder #(.disabled("Z"), .enable("false"), .select(4)) decoder_2 (
    .out0(OFlags[0]), .out1(OFlags[1]), .out2(OFlags[2]), .out3(OFlags[3]), .out4(OFlags[4]),
    .out5(OFlags[5]), .out6(OFlags[6]), .out7(OFlags[7]), .out8(OFlags[8]), .out9(OFlags[9]),
    .out10(OFlags[10]), .out11(OFlags[11]), .out12(OFlags[12]), .out13(OFlags[13]), .out14(OFlags[14]),
    .out15(OFlags[15]), .sel(in_1[3:0]));

  assign Data = in_1[15:8];

  // Notes on the sheet:
  //   in_1: pull=down
endmodule

module ALU (
  input  [7:0] A,
  input  [7:0] B,
  input  [7:0] Flags,
  output [7:0] out_4
);

  wire demultiplexer_1_out0, demultiplexer_1_out1, demultiplexer_1_out2, demultiplexer_1_out3,
       demultiplexer_1_out4, or_2_out;
  wire [7:0] and_1_out, eightbitadder_1_sum, or_1_out;

  Demultiplexer #(.select(3)) demultiplexer_1 (
    .out0(demultiplexer_1_out0), .out1(demultiplexer_1_out1), .out2(demultiplexer_1_out2),
    .out3(demultiplexer_1_out3), .out4(demultiplexer_1_out4), .in(1'b1), .sel(Flags[2:0]));  // open: out5, out6, out7
  assign or_1_out = B | A;  // OR_Gate or_1, 8 bits wide
  assign and_1_out = B & A;  // AND_Gate and_1, 8 bits wide
  assign out_4 = demultiplexer_1_out2 ? and_1_out : 8'bz;  // Controlled_Buffer controlled_buffer_1
  EightBitAdder eightbitadder_1 (
    .A(A), .B(B), .Subtract(demultiplexer_1_out1), .SUM(eightbitadder_1_sum));  // open: Cin, Co
  assign out_4 = or_2_out ? eightbitadder_1_sum : 8'bz;  // Controlled_Buffer controlled_buffer_2
  or or_2 (or_2_out, demultiplexer_1_out0, demultiplexer_1_out1);
  assign out_4 = demultiplexer_1_out4 ? ~A : 8'bz;  // Controlled_Inverter controlled_inverter_1
  assign out_4 = demultiplexer_1_out3 ? or_1_out : 8'bz;  // Controlled_Buffer controlled_buffer_3

  // Notes on the sheet:
  //   Flag Decoder
endmodule

module SixteenBitAdder (
  input  [15:0] in_1,
  input  [15:0] in_2,
  input  [15:0] in_3,
  input  in_4
);

  wire eightbitadder_1_co;

  EightBitAdder eightbitadder_1 (
    .A(in_1[7:0]), .B(in_3[7:0]), .Subtract(1'b0), .Cin(in_4), .Co(eightbitadder_1_co), .SUM(in_2[15:8]));
  EightBitAdder eightbitadder_2 (
    .A(in_1[15:8]), .B(in_3[15:8]), .Subtract(1'b0), .Cin(eightbitadder_1_co), .SUM(in_2[7:0]));  // open: Co
endmodule
